// Logisim project hw4.circ as structural Verilog: 7 circuits, main circuit main
module main (
  input  write_enable,
  input  reset
);

  wire clk_out, memorylatch_1_oe_latched, memorylatch_1_we_latched, not_1_out;
  wire [2:0] multiplexer_1_out, splitting_bits_1_rd, splitting_bits_1_rs, splitting_bits_1_rt,
       splitting_bits_1_shamt;
  wire [5:0] splitting_bits_1_immed;
  wire [15:0] alu_1_data_out, alu_2_data_out, bit_extender_1_out, bit_extender_2_out,
       Data_Memory_704a74f6_dout, Instruction_Memory_b2d019ad_data, memorylatch_1_address_latched,
       memorylatch_1_data_in_latched, multiplexer_2_out, multiplexer_3_out, PC_data_out,
       registerfile_1_rs1_out, registerfile_1_rs2_out;

  Clock clk (.out(clk_out));
  CreateRegister PC (
    .reset(reset), .clk(clk_out), .write_en(write_enable), .data_in(alu_1_data_out), .data_out(PC_data_out));
  ALU alu_1 (.A(PC_data_out), .B(16'h4), .Opcode(4'b1000), .data_out(alu_1_data_out));
  ROM #(.addrWidth(16), .dataWidth(16)) Instruction_Memory_b2d019ad (
    .addr(PC_data_out), .data(Instruction_Memory_b2d019ad_data));
  not not_1 (not_1_out, clk_out);
  RegisterFile registerfile_1 (
    .rd(multiplexer_1_out), .data_in(multiplexer_3_out), .clk(not_1_out), .reset(reset),
    .rs1(splitting_bits_1_rs), .rs2(splitting_bits_1_rt), .rs2_out(registerfile_1_rs2_out),
    .rs1_out(registerfile_1_rs1_out));  // open: wr_enable
  Multiplexer #(.width(3), .enable("false")) multiplexer_1 (
    .in0(splitting_bits_1_rt), .in1(splitting_bits_1_rd), .out(multiplexer_1_out));  // open: sel
  Splitting_Bits splitting_bits_1 (
    .data_in(Instruction_Memory_b2d019ad_data), .rs(splitting_bits_1_rs), .rt(splitting_bits_1_rt),
    .rd(splitting_bits_1_rd), .shamt(splitting_bits_1_shamt), .immed(splitting_bits_1_immed));  // open: opcode, address
  assign bit_extender_1_out = {{13{splitting_bits_1_shamt[2]}}, splitting_bits_1_shamt};  // Bit_Extender bit_extender_1
  assign bit_extender_2_out = {{10{splitting_bits_1_immed[5]}}, splitting_bits_1_immed};  // Bit_Extender bit_extender_2
  Multiplexer #(.select(2), .width(16), .enable("false")) multiplexer_2 (
    .in0(registerfile_1_rs2_out), .in1(bit_extender_1_out), .in2(bit_extender_2_out), .out(multiplexer_2_out));  // open: in3, sel
  ALU alu_2 (.A(registerfile_1_rs1_out), .B(multiplexer_2_out), .data_out(alu_2_data_out));  // open: Opcode
  RAM #(.addrWidth(16), .dataWidth(16), .trigger("high"), .databus("bibus")) Data_Memory_704a74f6 (
    .addr(memorylatch_1_address_latched), .we(memorylatch_1_we_latched), .oe(memorylatch_1_oe_latched),
    .din(memorylatch_1_data_in_latched), .dout(Data_Memory_704a74f6_dout));
  MemoryLatch memorylatch_1 (
    .address(alu_2_data_out), .WE(write_enable), .clk(clk_out), .data_in(registerfile_1_rs2_out),
    .address_latched(memorylatch_1_address_latched), .WE_latched(memorylatch_1_we_latched),
    .OE_latched(memorylatch_1_oe_latched), .data_in_latched(memorylatch_1_data_in_latched));
  Multiplexer #(.width(16), .enable("false")) multiplexer_3 (
    .in0(alu_2_data_out), .in1(Data_Memory_704a74f6_dout), .out(multiplexer_3_out));  // open: sel
endmodule

module RegisterFile (
  input  [2:0] rd,
  input  wr_enable,
  input  [15:0] data_in,
  input  clk,
  input  reset,
  input  [2:0] rs1,
  input  [2:0] rs2,
  output [15:0] rs2_out,
  output [15:0] rs1_out
);

  wire decoder_1_out0, decoder_1_out1, decoder_1_out2, decoder_1_out3, decoder_1_out4, decoder_1_out5,
       decoder_1_out6, decoder_1_out7, decoder_2_out0, decoder_2_out1, decoder_2_out2, decoder_2_out3,
       decoder_2_out4, decoder_2_out5, decoder_2_out6, decoder_2_out7, decoder_3_out0, decoder_3_out1,
       decoder_3_out2, decoder_3_out3, decoder_3_out4, decoder_3_out5, decoder_3_out6, decoder_3_out7;
  wire [15:0] createregister_1_data_out, createregister_2_data_out, createregister_3_data_out,
       createregister_4_data_out, createregister_5_data_out, createregister_6_data_out,
       createregister_7_data_out, createregister_8_data_out;

  Decoder #(.select(3)) decoder_1 (
    .out0(decoder_1_out0), .out1(decoder_1_out1), .out2(decoder_1_out2), .out3(decoder_1_out3),
    .out4(decoder_1_out4), .out5(decoder_1_out5), .out6(decoder_1_out6), .out7(decoder_1_out7), .sel(rd),
    .en(wr_enable));
  CreateRegister createregister_1 (
    .reset(reset), .clk(clk), .write_en(decoder_1_out0), .data_in(data_in),
    .data_out(createregister_1_data_out));
  // Probe on createregister_1_data_out
  CreateRegister createregister_2 (
    .reset(reset), .clk(clk), .write_en(decoder_1_out1), .data_in(data_in),
    .data_out(createregister_2_data_out));
  // Probe on createregister_2_data_out
  CreateRegister createregister_3 (
    .reset(reset), .clk(clk), .write_en(decoder_1_out3), .data_in(data_in),
    .data_out(createregister_3_data_out));
  CreateRegister createregister_4 (
    .reset(reset), .clk(clk), .write_en(decoder_1_out2), .data_in(data_in),
    .data_out(createregister_4_data_out));
  // Probe on createregister_4_data_out
  CreateRegister createregister_5 (
    .reset(reset), .clk(clk), .write_en(decoder_1_out4), .data_in(data_in),
    .data_out(createregister_5_data_out));
  // Probe on createregister_3_data_out
  CreateRegister createregister_6 (
    .reset(reset), .clk(clk), .write_en(decoder_1_out5), .data_in(data_in),
    .data_out(createregister_6_data_out));
  // Probe on createregister_6_data_out
  // Probe on createregister_5_data_out
  CreateRegister createregister_7 (
    .reset(reset), .clk(clk), .write_en(decoder_1_out6), .data_in(data_in),
    .data_out(createregister_7_data_out));
  // Probe on createregister_7_data_out
  CreateRegister createregister_8 (
    .reset(reset), .clk(clk), .write_en(decoder_1_out7), .data_in(data_in),
    .data_out(createregister_8_data_out));
  // Probe on createregister_8_data_out
  Decoder #(.select(3)) decoder_2 (
    .out0(decoder_2_out0), .out1(decoder_2_out1), .out2(decoder_2_out2), .out3(decoder_2_out3),
    .out4(decoder_2_out4), .out5(decoder_2_out5), .out6(decoder_2_out6), .out7(decoder_2_out7), .sel(rs1));  // open: en
  assign rs1_out = decoder_2_out2 ? createregister_4_data_out : 16'bz;  // Controlled_Buffer controlled_buffer_1
  assign rs1_out = decoder_2_out1 ? createregister_2_data_out : 16'bz;  // Controlled_Buffer controlled_buffer_2
  assign rs1_out = decoder_2_out0 ? createregister_1_data_out : 16'bz;  // Controlled_Buffer controlled_buffer_3
  assign rs1_out = decoder_2_out6 ? createregister_7_data_out : 16'bz;  // Controlled_Buffer controlled_buffer_4
  assign rs1_out = decoder_2_out5 ? createregister_6_data_out : 16'bz;  // Controlled_Buffer controlled_buffer_5
  assign rs1_out = decoder_2_out4 ? createregister_5_data_out : 16'bz;  // Controlled_Buffer controlled_buffer_6
  assign rs1_out = decoder_2_out3 ? createregister_3_data_out : 16'bz;  // Controlled_Buffer controlled_buffer_7
  assign rs2_out = decoder_3_out2 ? createregister_4_data_out : 16'bz;  // Controlled_Buffer controlled_buffer_8
  assign rs2_out = decoder_3_out1 ? createregister_2_data_out : 16'bz;  // Controlled_Buffer controlled_buffer_9
  assign rs2_out = decoder_3_out0 ? createregister_1_data_out : 16'bz;  // Controlled_Buffer controlled_buffer_10
  assign rs1_out = decoder_2_out7 ? createregister_8_data_out : 16'bz;  // Controlled_Buffer controlled_buffer_11
  Decoder #(.select(3)) decoder_3 (
    .out0(decoder_3_out0), .out1(decoder_3_out1), .out2(decoder_3_out2), .out3(decoder_3_out3),
    .out4(decoder_3_out4), .out5(decoder_3_out5), .out6(decoder_3_out6), .out7(decoder_3_out7), .sel(rs2));  // open: en
  assign rs2_out = decoder_3_out6 ? createregister_7_data_out : 16'bz;  // Controlled_Buffer controlled_buffer_12
  assign rs2_out = decoder_3_out5 ? createregister_6_data_out : 16'bz;  // Controlled_Buffer controlled_buffer_13
  assign rs2_out = decoder_3_out4 ? createregister_5_data_out : 16'bz;  // Controlled_Buffer controlled_buffer_14
  assign rs2_out = decoder_3_out3 ? createregister_3_data_out : 16'bz;  // Controlled_Buffer controlled_buffer_15
  assign rs2_out = decoder_3_out7 ? createregister_8_data_out : 16'bz;  // Controlled_Buffer controlled_buffer_16
endmodule

module CreateRegister (
  input  reset,
  input  clk,
  input  write_en,
  input  [15:0] data_in,
  output [15:0] data_out
);

  wire and_1_out;

  and and_1 (and_1_out, clk, write_en);
  D_Flip_Flop d_ff_1 (.D(data_in[0]), .clk(and_1_out), .Q(data_out[0]), .reset(reset));  // open: Qn, preset
  D_Flip_Flop d_ff_2 (.D(data_in[1]), .clk(and_1_out), .Q(data_out[1]), .reset(reset));  // open: Qn, preset
  D_Flip_Flop d_ff_3 (.D(data_in[2]), .clk(and_1_out), .Q(data_out[2]), .reset(reset));  // open: Qn, preset
  D_Flip_Flop d_ff_4 (.D(data_in[3]), .clk(and_1_out), .Q(data_out[3]), .reset(reset));  // open: Qn, preset
  D_Flip_Flop d_ff_5 (.D(data_in[4]), .clk(and_1_out), .Q(data_out[4]), .reset(reset));  // open: Qn, preset
  D_Flip_Flop d_ff_6 (.D(data_in[5]), .clk(and_1_out), .Q(data_out[5]), .reset(reset));  // open: Qn, preset
  D_Flip_Flop d_ff_7 (.D(data_in[6]), .clk(and_1_out), .Q(data_out[6]), .reset(reset));  // open: Qn, preset
  D_Flip_Flop d_ff_8 (.D(data_in[7]), .clk(and_1_out), .Q(data_out[7]), .reset(reset));  // open: Qn, preset
  D_Flip_Flop d_ff_9 (.D(data_in[8]), .clk(and_1_out), .Q(data_out[8]), .reset(reset));  // open: Qn, preset
  D_Flip_Flop d_ff_10 (.D(data_in[9]), .clk(and_1_out), .Q(data_out[9]), .reset(reset));  // open: Qn, preset
  D_Flip_Flop d_ff_11 (.D(data_in[10]), .clk(and_1_out), .Q(data_out[10]), .reset(reset));  // open: Qn, preset
  D_Flip_Flop d_ff_12 (.D(data_in[11]), .clk(and_1_out), .Q(data_out[11]), .reset(reset));  // open: Qn, preset
  D_Flip_Flop d_ff_13 (.D(data_in[12]), .clk(and_1_out), .Q(data_out[12]), .reset(reset));  // open: Qn, preset
  D_Flip_Flop d_ff_14 (.D(data_in[13]), .clk(and_1_out), .Q(data_out[13]), .reset(reset));  // open: Qn, preset
  D_Flip_Flop d_ff_15 (.D(data_in[14]), .clk(and_1_out), .Q(data_out[14]), .reset(reset));  // open: Qn, preset
  D_Flip_Flop d_ff_16 (.D(data_in[15]), .clk(and_1_out), .Q(data_out[15]), .reset(reset));  // open: Qn, preset

  // Notes on the sheet:
  //   clk: pull=up
endmodule

module MemoryLatch (
  input  [15:0] address,
  input  WE,
  input  clk,
  input  [15:0] data_in,
  output [15:0] address_latched,
  output WE_latched,
  output OE_latched,
  output [15:0] data_in_latched
);

  wire d_ff_1_q;
  wire [15:0] register_1_q;

  Register #(.width(16), .trigger("falling")) register_1 (
    .D(address), .en(WE), .clk(clk), .Q(register_1_q));  // open: clr
  Register #(.width(16), .trigger("falling")) register_2 (
    .D(data_in), .en(WE), .clk(clk), .Q(data_in_latched));  // open: clr
  D_Flip_Flop #(.trigger("falling")) d_ff_1 (.D(WE), .clk(clk), .Q(d_ff_1_q));  // open: Qn, preset, reset
  Multiplexer #(.width(16), .enable("false")) multiplexer_1 (
    .in0(address), .in1(register_1_q), .out(address_latched), .sel(d_ff_1_q));
  and and_1 (WE_latched, clk, d_ff_1_q);
  not not_1 (OE_latched, WE_latched);
endmodule

module ALU (
  input  [15:0] A,
  input  [15:0] B,
  input  [3:0] Opcode,
  output [15:0] data_out
);

  wire [15:0] adder_1_out, and_1_out, or_1_out, subtractor_1_out;

  Adder #(.width(16)) adder_1 (.a(A), .b(B), .out(adder_1_out));  // open: cin, cout
  Subtractor #(.width(16)) subtractor_1 (.a(A), .b(B), .out(subtractor_1_out));  // open: bin, bout
  assign and_1_out = A & B;  // AND_Gate and_1, 16 bits wide
  assign or_1_out = A | B;  // OR_Gate or_1, 16 bits wide
  Multiplexer #(.select(4), .width(16), .enable("false")) multiplexer_1 (
    .in6(or_1_out), .in7(and_1_out), .in8(adder_1_out), .in9(adder_1_out), .in10(subtractor_1_out),
    .out(data_out), .sel(Opcode));  // open: in0, in1, in2, in3, in4, in5, in11, in12, in13, in14, in15
endmodule

module InstructionDecoder (
);

  wire [3:0] opcode;

  Decoder #(.select(4)) decoder_1 (.sel(opcode));  // open: out0, out1, out2, out3, out4, out5, out6, out7, out8, out9, out10, out11, out12, out13, out14, out15, en
endmodule

module Splitting_Bits (
  input  [15:0] data_in,
  output [2:0] rd,
  output [2:0] shamt,
  output [2:0] rs,
  output [2:0] rt,
  output [5:0] immed,
  output [3:0] opcode,
  output [11:0] address
);


  assign address = data_in[15:4];
  assign immed = data_in[15:10];
  assign opcode = data_in[3:0];
  assign rd = data_in[12:10];
  assign rs = data_in[6:4];
  assign rt = data_in[9:7];
  assign shamt = data_in[15:13];
endmodule
